# Fritzing sketch _Sketch (saved by Fritzing 1.0.6)

parts:
  A1 = Esp32-c3 super mini
  U2 = WS2812 RGB LED strip
  DS1 = DS18B20 1-Wire Temperature Sensor Probe
  KY-3 = Keyes Relay [package=THT]
  KY-2 = Keyes Relay [package=THT]
  KY-1 = Keyes Relay [package=THT]
  R1 = Resistor [tolerance=±5% resistance=4.7k package="0603 [SMD]"]  # not connected

nets:
  N1: A1.Pin_1, KY-1.signal
  N2: A1.Pin_2, KY-2.signal
  N3: A1.Pin_3, KY-3.signal
  N4: A1.Pin_11, DS1.DQ
  N5: A1.Pin_12, U2.DOUT
  N6: A1.Pin_15, U2.GND
  N7: A1.Pin_16, U2.VCC

custom parts:
  Esp32-c3 super mini: ESP32-C3 Development Board ESP32 SuperMini Development Board ESP32 Development Board WiFi Bluetooth.
  WS2812 RGB LED strip: WS2812 strip
  Keyes Relay: The Keyes 5V relay module is suitable for SCM development, home appliance control. It uses a 5V~12V TIL control signal which can control DC / AC signal.
